// Logisim project ALU.circ as structural Verilog: 5 circuits, main circuit main
module main (
  input  B7,
  input  B6,
  input  B5,
  input  B4,
  input  B3,
  input  B2,
  input  B1,
  input  B0,
  input  A7,
  input  A6,
  input  A5,
  input  A4,
  input  A3,
  input  A2,
  input  A1,
  input  A0,
  output out_17,
  output out_18,
  output out_19,
  output out_20,
  output out_21,
  output out_22,
  output out_23,
  output out_24,
  output P7,
  output P6,
  output P5,
  output P4,
  output P3,
  output P2,
  output P1,
  output P0
);

  wire and_1_out, and_2_out, and_3_out, and_4_out, and_5_out, and_6_out, and_7_out, and_8_out, and_9_out,
       and_10_out, and_11_out, and_12_out, and_13_out, and_14_out, and_15_out, and_16_out, and_17_out,
       and_18_out, and_19_out, and_20_out, and_21_out, and_22_out, and_23_out, and_24_out, and_25_out,
       and_26_out, and_27_out, and_28_out, and_29_out, and_30_out, and_31_out, and_32_out, and_33_out,
       and_34_out, and_35_out, and_36_out, and_37_out, and_38_out, and_39_out, and_40_out, and_41_out,
       and_42_out, and_43_out, and_44_out, and_45_out, and_46_out, and_47_out, and_48_out, and_49_out,
       and_50_out, and_51_out, and_52_out, and_53_out, and_54_out, and_55_out, and_56_out, and_57_out,
       and_58_out, and_59_out, and_60_out, and_61_out, and_62_out, and_63_out, n8_bit_adder_2_co,
       n8_bit_adder_2_s1, n8_bit_adder_2_s2, n8_bit_adder_2_s3, n8_bit_adder_2_s4, n8_bit_adder_2_s5,
       n8_bit_adder_2_s6, n8_bit_adder_2_s7, n8_bit_adder_3_co, n8_bit_adder_3_s1, n8_bit_adder_3_s2,
       n8_bit_adder_3_s3, n8_bit_adder_3_s4, n8_bit_adder_3_s5, n8_bit_adder_3_s6, n8_bit_adder_3_s7,
       n8_bit_adder_4_co, n8_bit_adder_4_s1, n8_bit_adder_4_s2, n8_bit_adder_4_s3, n8_bit_adder_4_s4,
       n8_bit_adder_4_s5, n8_bit_adder_4_s6, n8_bit_adder_4_s7, n8_bit_adder_5_co, n8_bit_adder_5_s1,
       n8_bit_adder_5_s2, n8_bit_adder_5_s3, n8_bit_adder_5_s4, n8_bit_adder_5_s5, n8_bit_adder_5_s6,
       n8_bit_adder_5_s7, n8_bit_adder_6_co, n8_bit_adder_6_s1, n8_bit_adder_6_s2, n8_bit_adder_6_s3,
       n8_bit_adder_6_s4, n8_bit_adder_6_s5, n8_bit_adder_6_s6, n8_bit_adder_6_s7, n8_bit_adder_7_co,
       n8_bit_adder_7_s1, n8_bit_adder_7_s2, n8_bit_adder_7_s3, n8_bit_adder_7_s4, n8_bit_adder_7_s5,
       n8_bit_adder_7_s6, n8_bit_adder_7_s7;

  and and_1 (and_1_out, A7, B7);
  and and_2 (and_2_out, A7, B6);
  and and_3 (and_3_out, A7, B5);
  and and_4 (and_4_out, A7, B4);
  and and_5 (and_5_out, A7, B3);
  and and_6 (and_6_out, A7, B1);
  and and_7 (and_7_out, A7, B2);
  and and_8 (and_8_out, A7, B0);
  and and_9 (and_9_out, A6, B6);
  and and_10 (and_10_out, A6, B7);
  and and_11 (and_11_out, A6, B5);
  _8_bit_adder u_8_bit_adder_1 (
    .B0(n8_bit_adder_2_s1), .B1(n8_bit_adder_2_s2), .B2(n8_bit_adder_2_s3), .B3(n8_bit_adder_2_s4),
    .B4(n8_bit_adder_2_s5), .B5(n8_bit_adder_2_s6), .B6(n8_bit_adder_2_s7), .B7(n8_bit_adder_2_co),
    .A0(and_8_out), .A1(and_6_out), .A2(and_7_out), .A3(and_5_out), .A4(and_4_out), .A5(and_3_out),
    .A6(and_2_out), .A7(and_1_out), .Add_Sub(1'b0), .Co(out_17), .S0(P7), .S1(out_24), .S2(out_23),
    .S3(out_22), .S4(out_21), .S5(out_20), .S6(out_19), .S7(out_18));  // open: Zero, Negative, Overflow
  and and_12 (and_12_out, A6, B3);
  and and_13 (and_13_out, A6, B4);
  and and_14 (and_14_out, A6, B2);
  and and_15 (and_15_out, A6, B1);
  and and_16 (and_16_out, A6, B0);
  and and_17 (and_17_out, A5, B6);
  and and_18 (and_18_out, A5, B7);
  and and_19 (and_19_out, A5, B5);
  and and_20 (and_20_out, A5, B3);
  and and_21 (and_21_out, A5, B4);
  _8_bit_adder u_8_bit_adder_2 (
    .B0(n8_bit_adder_3_s1), .B1(n8_bit_adder_3_s2), .B2(n8_bit_adder_3_s3), .B3(n8_bit_adder_3_s4),
    .B4(n8_bit_adder_3_s5), .B5(n8_bit_adder_3_s6), .B6(n8_bit_adder_3_s7), .B7(n8_bit_adder_3_co),
    .A0(and_16_out), .A1(and_15_out), .A2(and_14_out), .A3(and_12_out), .A4(and_13_out), .A5(and_11_out),
    .A6(and_9_out), .A7(and_10_out), .Add_Sub(1'b0), .Co(n8_bit_adder_2_co), .S0(P6), .S1(n8_bit_adder_2_s1),
    .S2(n8_bit_adder_2_s2), .S3(n8_bit_adder_2_s3), .S4(n8_bit_adder_2_s4), .S5(n8_bit_adder_2_s5),
    .S6(n8_bit_adder_2_s6), .S7(n8_bit_adder_2_s7));  // open: Zero, Negative, Overflow
  and and_22 (and_22_out, A5, B1);
  and and_23 (and_23_out, A5, B2);
  and and_24 (and_24_out, A5, B0);
  and and_25 (and_25_out, A4, B7);
  and and_26 (and_26_out, A4, B5);
  and and_27 (and_27_out, A4, B6);
  and and_28 (and_28_out, A4, B4);
  _8_bit_adder u_8_bit_adder_3 (
    .B0(n8_bit_adder_4_s1), .B1(n8_bit_adder_4_s2), .B2(n8_bit_adder_4_s3), .B3(n8_bit_adder_4_s4),
    .B4(n8_bit_adder_4_s5), .B5(n8_bit_adder_4_s6), .B6(n8_bit_adder_4_s7), .B7(n8_bit_adder_4_co),
    .A0(and_24_out), .A1(and_22_out), .A2(and_23_out), .A3(and_20_out), .A4(and_21_out), .A5(and_19_out),
    .A6(and_17_out), .A7(and_18_out), .Add_Sub(1'b0), .Co(n8_bit_adder_3_co), .S0(P5),
    .S1(n8_bit_adder_3_s1), .S2(n8_bit_adder_3_s2), .S3(n8_bit_adder_3_s3), .S4(n8_bit_adder_3_s4),
    .S5(n8_bit_adder_3_s5), .S6(n8_bit_adder_3_s6), .S7(n8_bit_adder_3_s7));  // open: Zero, Negative, Overflow
  and and_29 (and_29_out, A4, B2);
  and and_30 (and_30_out, A4, B3);
  and and_31 (and_31_out, A4, B1);
  and and_32 (and_32_out, A4, B0);
  and and_33 (and_33_out, A3, B7);
  and and_34 (and_34_out, A3, B5);
  and and_35 (and_35_out, A3, B6);
  _8_bit_adder u_8_bit_adder_4 (
    .B0(n8_bit_adder_5_s1), .B1(n8_bit_adder_5_s2), .B2(n8_bit_adder_5_s3), .B3(n8_bit_adder_5_s4),
    .B4(n8_bit_adder_5_s5), .B5(n8_bit_adder_5_s6), .B6(n8_bit_adder_5_s7), .B7(n8_bit_adder_5_co),
    .A0(and_32_out), .A1(and_31_out), .A2(and_29_out), .A3(and_30_out), .A4(and_28_out), .A5(and_26_out),
    .A6(and_27_out), .A7(and_25_out), .Add_Sub(1'b0), .Co(n8_bit_adder_4_co), .S0(P4),
    .S1(n8_bit_adder_4_s1), .S2(n8_bit_adder_4_s2), .S3(n8_bit_adder_4_s3), .S4(n8_bit_adder_4_s4),
    .S5(n8_bit_adder_4_s5), .S6(n8_bit_adder_4_s6), .S7(n8_bit_adder_4_s7));  // open: Zero, Negative, Overflow
  and and_36 (and_36_out, A3, B3);
  and and_37 (and_37_out, A3, B4);
  and and_38 (and_38_out, A3, B1);
  and and_39 (and_39_out, A3, B2);
  and and_40 (and_40_out, A3, B0);
  and and_41 (and_41_out, A2, B6);
  and and_42 (and_42_out, A2, B7);
  _8_bit_adder u_8_bit_adder_5 (
    .B0(n8_bit_adder_6_s1), .B1(n8_bit_adder_6_s2), .B2(n8_bit_adder_6_s3), .B3(n8_bit_adder_6_s4),
    .B4(n8_bit_adder_6_s5), .B5(n8_bit_adder_6_s6), .B6(n8_bit_adder_6_s7), .B7(n8_bit_adder_6_co),
    .A0(and_40_out), .A1(and_38_out), .A2(and_39_out), .A3(and_36_out), .A4(and_37_out), .A5(and_34_out),
    .A6(and_35_out), .A7(and_33_out), .Add_Sub(1'b0), .Co(n8_bit_adder_5_co), .S0(P3),
    .S1(n8_bit_adder_5_s1), .S2(n8_bit_adder_5_s2), .S3(n8_bit_adder_5_s3), .S4(n8_bit_adder_5_s4),
    .S5(n8_bit_adder_5_s5), .S6(n8_bit_adder_5_s6), .S7(n8_bit_adder_5_s7));  // open: Zero, Negative, Overflow
  and and_43 (and_43_out, A2, B4);
  and and_44 (and_44_out, A2, B5);
  and and_45 (and_45_out, A2, B3);
  and and_46 (and_46_out, A2, B1);
  and and_47 (and_47_out, A2, B2);
  and and_48 (and_48_out, A2, B0);
  and and_49 (and_49_out, A1, B7);
  and and_50 (and_50_out, A1, B6);
  and and_51 (and_51_out, A1, B5);
  _8_bit_adder u_8_bit_adder_6 (
    .B0(n8_bit_adder_7_s1), .B1(n8_bit_adder_7_s2), .B2(n8_bit_adder_7_s3), .B3(n8_bit_adder_7_s4),
    .B4(n8_bit_adder_7_s5), .B5(n8_bit_adder_7_s6), .B6(n8_bit_adder_7_s7), .B7(n8_bit_adder_7_co),
    .A0(and_48_out), .A1(and_46_out), .A2(and_47_out), .A3(and_45_out), .A4(and_43_out), .A5(and_44_out),
    .A6(and_41_out), .A7(and_42_out), .Add_Sub(1'b0), .Co(n8_bit_adder_6_co), .S0(P2),
    .S1(n8_bit_adder_6_s1), .S2(n8_bit_adder_6_s2), .S3(n8_bit_adder_6_s3), .S4(n8_bit_adder_6_s4),
    .S5(n8_bit_adder_6_s5), .S6(n8_bit_adder_6_s6), .S7(n8_bit_adder_6_s7));  // open: Zero, Negative, Overflow
  and and_52 (and_52_out, A1, B2);
  and and_53 (and_53_out, A1, B4);
  and and_54 (and_54_out, A1, B3);
  and and_55 (and_55_out, A1, B0);
  and and_56 (and_56_out, A1, B1);
  and and_57 (and_57_out, A0, B6);
  and and_58 (and_58_out, A0, B7);
  _8_bit_adder u_8_bit_adder_7 (
    .B0(and_63_out), .B1(and_62_out), .B2(and_59_out), .B3(and_60_out), .B4(and_61_out), .B5(and_57_out),
    .B6(and_58_out), .B7(1'b0), .A0(and_55_out), .A1(and_56_out), .A2(and_52_out), .A3(and_54_out),
    .A4(and_53_out), .A5(and_51_out), .A6(and_50_out), .A7(and_49_out), .Add_Sub(1'b0),
    .Co(n8_bit_adder_7_co), .S0(P1), .S1(n8_bit_adder_7_s1), .S2(n8_bit_adder_7_s2), .S3(n8_bit_adder_7_s3),
    .S4(n8_bit_adder_7_s4), .S5(n8_bit_adder_7_s5), .S6(n8_bit_adder_7_s6), .S7(n8_bit_adder_7_s7));  // open: Zero, Negative, Overflow
  and and_59 (and_59_out, A0, B3);
  and and_60 (and_60_out, A0, B4);
  and and_61 (and_61_out, A0, B5);
  and and_62 (and_62_out, A0, B2);
  and and_63 (and_63_out, A0, B1);
  and and_64 (P0, A0, B0);
endmodule

module _8_bit_adder (
  input  Add_Sub,
  input  B0,
  input  B1,
  input  B2,
  input  B3,
  input  B4,
  input  B5,
  input  B6,
  input  B7,
  input  A0,
  input  A1,
  input  A2,
  input  A3,
  input  A4,
  input  A5,
  input  A6,
  input  A7,
  output S0,
  output S1,
  output S2,
  output S3,
  output S4,
  output S5,
  output S6,
  output S7,
  output Zero,
  output Negative,
  output Overflow,
  output Co
);

  wire adder_1_co, adder_2_co, adder_3_co, adder_4_co, adder_5_co, adder_6_co, adder_7_co, and_1_out,
       and_2_out, not_1_out, not_2_out, not_3_out, or_2_out, xor_1_out, xor_2_out, xor_3_out, xor_4_out,
       xor_5_out, xor_6_out, xor_7_out, xor_8_out;

  xor xor_1 (xor_1_out, Add_Sub, B0);
  xor xor_2 (xor_2_out, Add_Sub, B1);
  xor xor_3 (xor_3_out, Add_Sub, B2);
  xor xor_4 (xor_4_out, Add_Sub, B3);
  xor xor_5 (xor_5_out, Add_Sub, B4);
  xor xor_6 (xor_6_out, Add_Sub, B5);
  xor xor_7 (xor_7_out, Add_Sub, B6);
  xor xor_8 (xor_8_out, Add_Sub, B7);
  not not_1 (not_1_out, xor_8_out);
  not not_2 (not_2_out, A7);
  not not_3 (not_3_out, Negative);
  Adder adder_1 (.A(xor_1_out), .B(A0), .Ci(Add_Sub), .Co(adder_1_co), .S(S0));
  Adder adder_2 (.A(xor_2_out), .B(A1), .Ci(adder_1_co), .Co(adder_2_co), .S(S1));
  Adder adder_3 (.A(xor_3_out), .B(A2), .Ci(adder_2_co), .Co(adder_3_co), .S(S2));
  Adder adder_4 (.A(xor_4_out), .B(A3), .Ci(adder_3_co), .Co(adder_4_co), .S(S3));
  Adder adder_5 (.A(xor_5_out), .B(A4), .Ci(adder_4_co), .Co(adder_5_co), .S(S4));
  Adder adder_6 (.A(xor_6_out), .B(A5), .Ci(adder_5_co), .Co(adder_6_co), .S(S5));
  Adder adder_7 (.A(xor_7_out), .B(A6), .Ci(adder_6_co), .Co(adder_7_co), .S(S6));
  Adder adder_8 (.A(xor_8_out), .B(A7), .Ci(adder_7_co), .Co(Co), .S(Negative));
  and and_1 (and_1_out, not_3_out, xor_8_out, A7);
  and and_2 (and_2_out, Negative, not_2_out, not_1_out);
  or or_1 (Overflow, and_1_out, and_2_out);
  not not_4 (Zero, or_2_out);
  or or_2 (or_2_out, S0, S1, S2, S3, S4, S5, S6, Negative);

  assign S7 = Negative;
endmodule

module Divider (
  input  A7,
  input  A6,
  input  A5,
  input  A4,
  input  A3,
  input  A2,
  input  A1,
  input  A0,
  input  B7,
  input  B6,
  input  B5,
  input  B4,
  input  B3,
  input  B2,
  input  B1,
  input  B0,
  output Q8,
  output Q7,
  output Q6,
  output Q5,
  output Q4,
  output Q3,
  output Q2,
  output Q1,
  output R7,
  output R6,
  output R5,
  output R4,
  output R3,
  output R2,
  output R1,
  output R0
);

  wire multiplexer_1_out_19, multiplexer_1_out_20, multiplexer_1_out_21, multiplexer_1_out_22,
       multiplexer_1_out_23, multiplexer_1_out_24, multiplexer_1_out_25, multiplexer_2_out_19,
       multiplexer_2_out_20, multiplexer_2_out_21, multiplexer_2_out_22, multiplexer_2_out_23,
       multiplexer_2_out_24, multiplexer_2_out_25, multiplexer_3_out_19, multiplexer_3_out_20,
       multiplexer_3_out_21, multiplexer_3_out_22, multiplexer_3_out_23, multiplexer_3_out_24,
       multiplexer_3_out_25, multiplexer_4_out_19, multiplexer_4_out_20, multiplexer_4_out_21,
       multiplexer_4_out_22, multiplexer_4_out_23, multiplexer_4_out_24, multiplexer_4_out_25,
       multiplexer_5_out_19, multiplexer_5_out_20, multiplexer_5_out_21, multiplexer_5_out_22,
       multiplexer_5_out_23, multiplexer_5_out_24, multiplexer_5_out_25, multiplexer_6_out_19,
       multiplexer_6_out_20, multiplexer_6_out_21, multiplexer_6_out_22, multiplexer_6_out_23,
       multiplexer_6_out_24, multiplexer_6_out_25, multiplexer_7_out_19, multiplexer_7_out_20,
       multiplexer_7_out_21, multiplexer_7_out_22, multiplexer_7_out_23, multiplexer_7_out_24,
       multiplexer_7_out_25, n8_bit_adder_1_s0, n8_bit_adder_1_s1, n8_bit_adder_1_s2, n8_bit_adder_1_s3,
       n8_bit_adder_1_s4, n8_bit_adder_1_s5, n8_bit_adder_1_s6, n8_bit_adder_1_s7, n8_bit_adder_2_s0,
       n8_bit_adder_2_s1, n8_bit_adder_2_s2, n8_bit_adder_2_s3, n8_bit_adder_2_s4, n8_bit_adder_2_s5,
       n8_bit_adder_2_s6, n8_bit_adder_2_s7, n8_bit_adder_3_s0, n8_bit_adder_3_s1, n8_bit_adder_3_s2,
       n8_bit_adder_3_s3, n8_bit_adder_3_s4, n8_bit_adder_3_s5, n8_bit_adder_3_s6, n8_bit_adder_3_s7,
       n8_bit_adder_4_s0, n8_bit_adder_4_s1, n8_bit_adder_4_s2, n8_bit_adder_4_s3, n8_bit_adder_4_s4,
       n8_bit_adder_4_s5, n8_bit_adder_4_s6, n8_bit_adder_4_s7, n8_bit_adder_5_s0, n8_bit_adder_5_s1,
       n8_bit_adder_5_s2, n8_bit_adder_5_s3, n8_bit_adder_5_s4, n8_bit_adder_5_s5, n8_bit_adder_5_s6,
       n8_bit_adder_5_s7, n8_bit_adder_6_s0, n8_bit_adder_6_s1, n8_bit_adder_6_s2, n8_bit_adder_6_s3,
       n8_bit_adder_6_s4, n8_bit_adder_6_s5, n8_bit_adder_6_s6, n8_bit_adder_6_s7, n8_bit_adder_7_s0,
       n8_bit_adder_7_s1, n8_bit_adder_7_s2, n8_bit_adder_7_s3, n8_bit_adder_7_s4, n8_bit_adder_7_s5,
       n8_bit_adder_7_s6, n8_bit_adder_7_s7, n8_bit_adder_8_s0, n8_bit_adder_8_s1, n8_bit_adder_8_s2,
       n8_bit_adder_8_s3, n8_bit_adder_8_s4, n8_bit_adder_8_s5, n8_bit_adder_8_s6, n8_bit_adder_8_s7;

  Multiplexer multiplexer_1 (
    .in_17(Q8), .A7(1'b0), .A6(1'b0), .A5(1'b0), .A4(1'b0), .A3(1'b0), .A2(1'b0), .A1(1'b0), .A0(A7),
    .B7(n8_bit_adder_1_s7), .B6(n8_bit_adder_1_s6), .B5(n8_bit_adder_1_s5), .B4(n8_bit_adder_1_s4),
    .B3(n8_bit_adder_1_s3), .B2(n8_bit_adder_1_s2), .B1(n8_bit_adder_1_s1), .B0(n8_bit_adder_1_s0),
    .out_19(multiplexer_1_out_19), .out_20(multiplexer_1_out_20), .out_21(multiplexer_1_out_21),
    .out_22(multiplexer_1_out_22), .out_23(multiplexer_1_out_23), .out_24(multiplexer_1_out_24),
    .out_25(multiplexer_1_out_25));  // open: out_18
  Multiplexer multiplexer_2 (
    .in_17(Q7), .A7(multiplexer_1_out_19), .A6(multiplexer_1_out_20), .A5(multiplexer_1_out_21),
    .A4(multiplexer_1_out_22), .A3(multiplexer_1_out_23), .A2(multiplexer_1_out_24),
    .A1(multiplexer_1_out_25), .A0(A6), .B7(n8_bit_adder_2_s7), .B6(n8_bit_adder_2_s6),
    .B5(n8_bit_adder_2_s5), .B4(n8_bit_adder_2_s4), .B3(n8_bit_adder_2_s3), .B2(n8_bit_adder_2_s2),
    .B1(n8_bit_adder_2_s1), .B0(n8_bit_adder_2_s0), .out_19(multiplexer_2_out_19),
    .out_20(multiplexer_2_out_20), .out_21(multiplexer_2_out_21), .out_22(multiplexer_2_out_22),
    .out_23(multiplexer_2_out_23), .out_24(multiplexer_2_out_24), .out_25(multiplexer_2_out_25));  // open: out_18
  _8_bit_adder u_8_bit_adder_1 (
    .B0(B0), .B1(B1), .B2(B2), .B3(B3), .B4(B4), .B5(B5), .B6(B6), .B7(B7), .A0(A7), .A1(1'b0), .A2(1'b0),
    .A3(1'b0), .A4(1'b0), .A5(1'b0), .A6(1'b0), .A7(1'b0), .Add_Sub(1'b1), .Co(Q8), .S0(n8_bit_adder_1_s0),
    .S1(n8_bit_adder_1_s1), .S2(n8_bit_adder_1_s2), .S3(n8_bit_adder_1_s3), .S4(n8_bit_adder_1_s4),
    .S5(n8_bit_adder_1_s5), .S6(n8_bit_adder_1_s6), .S7(n8_bit_adder_1_s7));  // open: Zero, Negative, Overflow
  Multiplexer multiplexer_3 (
    .in_17(Q6), .A7(multiplexer_2_out_19), .A6(multiplexer_2_out_20), .A5(multiplexer_2_out_21),
    .A4(multiplexer_2_out_22), .A3(multiplexer_2_out_23), .A2(multiplexer_2_out_24),
    .A1(multiplexer_2_out_25), .A0(A5), .B7(n8_bit_adder_3_s7), .B6(n8_bit_adder_3_s6),
    .B5(n8_bit_adder_3_s5), .B4(n8_bit_adder_3_s4), .B3(n8_bit_adder_3_s3), .B2(n8_bit_adder_3_s2),
    .B1(n8_bit_adder_3_s1), .B0(n8_bit_adder_3_s0), .out_19(multiplexer_3_out_19),
    .out_20(multiplexer_3_out_20), .out_21(multiplexer_3_out_21), .out_22(multiplexer_3_out_22),
    .out_23(multiplexer_3_out_23), .out_24(multiplexer_3_out_24), .out_25(multiplexer_3_out_25));  // open: out_18
  _8_bit_adder u_8_bit_adder_2 (
    .B0(B0), .B1(B1), .B2(B2), .B3(B3), .B4(B4), .B5(B5), .B6(B6), .B7(B7), .A0(A6),
    .A1(multiplexer_1_out_25), .A2(multiplexer_1_out_24), .A3(multiplexer_1_out_23),
    .A4(multiplexer_1_out_22), .A5(multiplexer_1_out_21), .A6(multiplexer_1_out_20),
    .A7(multiplexer_1_out_19), .Add_Sub(1'b1), .Co(Q7), .S0(n8_bit_adder_2_s0), .S1(n8_bit_adder_2_s1),
    .S2(n8_bit_adder_2_s2), .S3(n8_bit_adder_2_s3), .S4(n8_bit_adder_2_s4), .S5(n8_bit_adder_2_s5),
    .S6(n8_bit_adder_2_s6), .S7(n8_bit_adder_2_s7));  // open: Zero, Negative, Overflow
  Multiplexer multiplexer_4 (
    .in_17(Q5), .A7(multiplexer_3_out_19), .A6(multiplexer_3_out_20), .A5(multiplexer_3_out_21),
    .A4(multiplexer_3_out_22), .A3(multiplexer_3_out_23), .A2(multiplexer_3_out_24),
    .A1(multiplexer_3_out_25), .A0(A4), .B7(n8_bit_adder_4_s7), .B6(n8_bit_adder_4_s6),
    .B5(n8_bit_adder_4_s5), .B4(n8_bit_adder_4_s4), .B3(n8_bit_adder_4_s3), .B2(n8_bit_adder_4_s2),
    .B1(n8_bit_adder_4_s1), .B0(n8_bit_adder_4_s0), .out_19(multiplexer_4_out_19),
    .out_20(multiplexer_4_out_20), .out_21(multiplexer_4_out_21), .out_22(multiplexer_4_out_22),
    .out_23(multiplexer_4_out_23), .out_24(multiplexer_4_out_24), .out_25(multiplexer_4_out_25));  // open: out_18
  _8_bit_adder u_8_bit_adder_3 (
    .B0(B0), .B1(B1), .B2(B2), .B3(B3), .B4(B4), .B5(B5), .B6(B6), .B7(B7), .A0(A5),
    .A1(multiplexer_2_out_25), .A2(multiplexer_2_out_24), .A3(multiplexer_2_out_23),
    .A4(multiplexer_2_out_22), .A5(multiplexer_2_out_21), .A6(multiplexer_2_out_20),
    .A7(multiplexer_2_out_19), .Add_Sub(1'b1), .Co(Q6), .S0(n8_bit_adder_3_s0), .S1(n8_bit_adder_3_s1),
    .S2(n8_bit_adder_3_s2), .S3(n8_bit_adder_3_s3), .S4(n8_bit_adder_3_s4), .S5(n8_bit_adder_3_s5),
    .S6(n8_bit_adder_3_s6), .S7(n8_bit_adder_3_s7));  // open: Zero, Negative, Overflow
  Multiplexer multiplexer_5 (
    .in_17(Q4), .A7(multiplexer_4_out_19), .A6(multiplexer_4_out_20), .A5(multiplexer_4_out_21),
    .A4(multiplexer_4_out_22), .A3(multiplexer_4_out_23), .A2(multiplexer_4_out_24),
    .A1(multiplexer_4_out_25), .A0(A3), .B7(n8_bit_adder_5_s7), .B6(n8_bit_adder_5_s6),
    .B5(n8_bit_adder_5_s5), .B4(n8_bit_adder_5_s4), .B3(n8_bit_adder_5_s3), .B2(n8_bit_adder_5_s2),
    .B1(n8_bit_adder_5_s1), .B0(n8_bit_adder_5_s0), .out_19(multiplexer_5_out_19),
    .out_20(multiplexer_5_out_20), .out_21(multiplexer_5_out_21), .out_22(multiplexer_5_out_22),
    .out_23(multiplexer_5_out_23), .out_24(multiplexer_5_out_24), .out_25(multiplexer_5_out_25));  // open: out_18
  _8_bit_adder u_8_bit_adder_4 (
    .B0(B0), .B1(B1), .B2(B2), .B3(B3), .B4(B4), .B5(B5), .B6(B6), .B7(B7), .A0(A4),
    .A1(multiplexer_3_out_25), .A2(multiplexer_3_out_24), .A3(multiplexer_3_out_23),
    .A4(multiplexer_3_out_22), .A5(multiplexer_3_out_21), .A6(multiplexer_3_out_20),
    .A7(multiplexer_3_out_19), .Add_Sub(1'b1), .Co(Q5), .S0(n8_bit_adder_4_s0), .S1(n8_bit_adder_4_s1),
    .S2(n8_bit_adder_4_s2), .S3(n8_bit_adder_4_s3), .S4(n8_bit_adder_4_s4), .S5(n8_bit_adder_4_s5),
    .S6(n8_bit_adder_4_s6), .S7(n8_bit_adder_4_s7));  // open: Zero, Negative, Overflow
  Multiplexer multiplexer_6 (
    .in_17(Q3), .A7(multiplexer_5_out_19), .A6(multiplexer_5_out_20), .A5(multiplexer_5_out_21),
    .A4(multiplexer_5_out_22), .A3(multiplexer_5_out_23), .A2(multiplexer_5_out_24),
    .A1(multiplexer_5_out_25), .A0(A2), .B7(n8_bit_adder_6_s7), .B6(n8_bit_adder_6_s6),
    .B5(n8_bit_adder_6_s5), .B4(n8_bit_adder_6_s4), .B3(n8_bit_adder_6_s3), .B2(n8_bit_adder_6_s2),
    .B1(n8_bit_adder_6_s1), .B0(n8_bit_adder_6_s0), .out_19(multiplexer_6_out_19),
    .out_20(multiplexer_6_out_20), .out_21(multiplexer_6_out_21), .out_22(multiplexer_6_out_22),
    .out_23(multiplexer_6_out_23), .out_24(multiplexer_6_out_24), .out_25(multiplexer_6_out_25));  // open: out_18
  _8_bit_adder u_8_bit_adder_5 (
    .B0(B0), .B1(B1), .B2(B2), .B3(B3), .B4(B4), .B5(B5), .B6(B6), .B7(B7), .A0(A3),
    .A1(multiplexer_4_out_25), .A2(multiplexer_4_out_24), .A3(multiplexer_4_out_23),
    .A4(multiplexer_4_out_22), .A5(multiplexer_4_out_21), .A6(multiplexer_4_out_20),
    .A7(multiplexer_4_out_19), .Add_Sub(1'b1), .Co(Q4), .S0(n8_bit_adder_5_s0), .S1(n8_bit_adder_5_s1),
    .S2(n8_bit_adder_5_s2), .S3(n8_bit_adder_5_s3), .S4(n8_bit_adder_5_s4), .S5(n8_bit_adder_5_s5),
    .S6(n8_bit_adder_5_s6), .S7(n8_bit_adder_5_s7));  // open: Zero, Negative, Overflow
  Multiplexer multiplexer_7 (
    .in_17(Q2), .A7(multiplexer_6_out_19), .A6(multiplexer_6_out_20), .A5(multiplexer_6_out_21),
    .A4(multiplexer_6_out_22), .A3(multiplexer_6_out_23), .A2(multiplexer_6_out_24),
    .A1(multiplexer_6_out_25), .A0(A1), .B7(n8_bit_adder_7_s7), .B6(n8_bit_adder_7_s6),
    .B5(n8_bit_adder_7_s5), .B4(n8_bit_adder_7_s4), .B3(n8_bit_adder_7_s3), .B2(n8_bit_adder_7_s2),
    .B1(n8_bit_adder_7_s1), .B0(n8_bit_adder_7_s0), .out_19(multiplexer_7_out_19),
    .out_20(multiplexer_7_out_20), .out_21(multiplexer_7_out_21), .out_22(multiplexer_7_out_22),
    .out_23(multiplexer_7_out_23), .out_24(multiplexer_7_out_24), .out_25(multiplexer_7_out_25));  // open: out_18
  _8_bit_adder u_8_bit_adder_6 (
    .B0(B0), .B1(B1), .B2(B2), .B3(B3), .B4(B4), .B5(B4), .B6(B6), .B7(B7), .A0(A2),
    .A1(multiplexer_5_out_25), .A2(multiplexer_5_out_24), .A3(multiplexer_5_out_23),
    .A4(multiplexer_5_out_22), .A5(multiplexer_5_out_21), .A6(multiplexer_5_out_20),
    .A7(multiplexer_5_out_19), .Add_Sub(1'b1), .Co(Q3), .S0(n8_bit_adder_6_s0), .S1(n8_bit_adder_6_s1),
    .S2(n8_bit_adder_6_s2), .S3(n8_bit_adder_6_s3), .S4(n8_bit_adder_6_s4), .S5(n8_bit_adder_6_s5),
    .S6(n8_bit_adder_6_s6), .S7(n8_bit_adder_6_s7));  // open: Zero, Negative, Overflow
  Multiplexer multiplexer_8 (
    .in_17(Q1), .A7(multiplexer_7_out_19), .A6(multiplexer_7_out_20), .A5(multiplexer_7_out_21),
    .A4(multiplexer_7_out_22), .A3(multiplexer_7_out_23), .A2(multiplexer_7_out_24),
    .A1(multiplexer_7_out_25), .A0(A0), .B7(n8_bit_adder_8_s7), .B6(n8_bit_adder_8_s6),
    .B5(n8_bit_adder_8_s5), .B4(n8_bit_adder_8_s4), .B3(n8_bit_adder_8_s3), .B2(n8_bit_adder_8_s2),
    .B1(n8_bit_adder_8_s1), .B0(n8_bit_adder_8_s0), .out_18(R7), .out_19(R6), .out_20(R5), .out_21(R4),
    .out_22(R3), .out_23(R2), .out_24(R1), .out_25(R0));
  _8_bit_adder u_8_bit_adder_7 (
    .B0(B0), .B1(B1), .B2(B2), .B3(B3), .B4(B4), .B5(B5), .B6(B6), .B7(B7), .A0(A1),
    .A1(multiplexer_6_out_25), .A2(multiplexer_6_out_24), .A3(multiplexer_6_out_23),
    .A4(multiplexer_6_out_22), .A5(multiplexer_6_out_21), .A6(multiplexer_6_out_20),
    .A7(multiplexer_6_out_19), .Add_Sub(1'b1), .Co(Q2), .S0(n8_bit_adder_7_s0), .S1(n8_bit_adder_7_s1),
    .S2(n8_bit_adder_7_s2), .S3(n8_bit_adder_7_s3), .S4(n8_bit_adder_7_s4), .S5(n8_bit_adder_7_s5),
    .S6(n8_bit_adder_7_s6), .S7(n8_bit_adder_7_s7));  // open: Zero, Negative, Overflow
  _8_bit_adder u_8_bit_adder_8 (
    .B0(B0), .B1(B1), .B2(B2), .B3(B3), .B4(B4), .B5(B5), .B6(B6), .B7(B7), .A0(A0),
    .A1(multiplexer_7_out_25), .A2(multiplexer_7_out_24), .A3(multiplexer_7_out_23),
    .A4(multiplexer_7_out_22), .A5(multiplexer_7_out_21), .A6(multiplexer_7_out_20),
    .A7(multiplexer_7_out_19), .Add_Sub(1'b1), .Co(Q1), .S0(n8_bit_adder_8_s0), .S1(n8_bit_adder_8_s1),
    .S2(n8_bit_adder_8_s2), .S3(n8_bit_adder_8_s3), .S4(n8_bit_adder_8_s4), .S5(n8_bit_adder_8_s5),
    .S6(n8_bit_adder_8_s6), .S7(n8_bit_adder_8_s7));  // open: Zero, Negative, Overflow
endmodule

module Adder (
  input  Ci,
  input  A,
  input  B,
  output S,
  output Co
);

  wire and_1_out, and_2_out, xor_1_out;

  xor xor_1 (xor_1_out, A, B);
  and and_1 (and_1_out, A, B);
  xor xor_2 (S, xor_1_out, Ci);
  and and_2 (and_2_out, xor_1_out, Ci);
  or or_1 (Co, and_2_out, and_1_out);
endmodule

module Multiplexer (
  input  A7,
  input  A6,
  input  A5,
  input  A4,
  input  A3,
  input  A2,
  input  A1,
  input  A0,
  input  B7,
  input  B6,
  input  B5,
  input  B4,
  input  B3,
  input  B2,
  input  B1,
  input  B0,
  input  in_17,
  output out_18,
  output out_19,
  output out_20,
  output out_21,
  output out_22,
  output out_23,
  output out_24,
  output out_25
);

  Multiplexer_part #(.enable("false")) multiplexer_1 (.in0(A7), .in1(B7), .out(out_18), .sel(in_17));
  Multiplexer_part #(.enable("false")) multiplexer_2 (.in0(A6), .in1(B6), .out(out_19), .sel(in_17));
  Multiplexer_part #(.enable("false")) multiplexer_3 (.in0(A5), .in1(B5), .out(out_20), .sel(in_17));
  Multiplexer_part #(.enable("false")) multiplexer_4 (.in0(A4), .in1(B4), .out(out_21), .sel(in_17));
  Multiplexer_part #(.enable("false")) multiplexer_5 (.in0(A3), .in1(B3), .out(out_22), .sel(in_17));
  Multiplexer_part #(.enable("false")) multiplexer_6 (.in0(A2), .in1(B2), .out(out_23), .sel(in_17));
  Multiplexer_part #(.enable("false")) multiplexer_7 (.in0(A1), .in1(B1), .out(out_24), .sel(in_17));
  Multiplexer_part #(.enable("false")) multiplexer_8 (.in0(A0), .in1(B0), .out(out_25), .sel(in_17));
endmodule
